// Logisim project 4-1 MUX.circ as structural Verilog
module _4_1_MUX (
  input  s1,
  input  s0,
  input  I0,
  input  I1,
  input  I2,
  input  I3,
  output Y
);

  wire and_1_out, and_2_out, and_3_out, and_4_out, not_1_out, not_2_out;

  not not_1 (not_1_out, s1);
  not not_2 (not_2_out, s0);
  and and_1 (and_1_out, not_2_out, not_1_out, I0);
  and and_2 (and_2_out, s0, not_1_out, I1);
  and and_3 (and_3_out, not_2_out, s1, I2);
  and and_4 (and_4_out, s0, s1, I3);
  or or_1 (Y, and_1_out, and_2_out, and_4_out, and_3_out);
endmodule

module lab02 (
  input  in_1,
  input  in_2,
  input  in_3,
  input  in_4,
  input  in_5,
  input  in_6,
  input  in_7,
  input  in_8,
  input  SQ,
  input  S1,
  input  CIN,
  input  in_12,
  input  in_13,
  input  in_14,
  input  A4,
  input  A3,
  input  A2,
  input  A1,
  input  in_19,
  output S8,
  output S7,
  output S6,
  output S5,
  output S4,
  output S3,
  output S1_2,
  output S0,
  output cout
);

  wire full_adder_1_carry, full_adder_2_carry, full_adder_3_carry, full_adder_4_carry, full_adder_5_carry,
       full_adder_6_carry, full_adder_7_carry, full_adder_8_carry, n4_1_mux_1_y, n4_1_mux_2_y, n4_1_mux_3_y,
       n4_1_mux_4_y, n4_1_mux_5_y, n4_1_mux_6_y, n4_1_mux_7_y, n4_1_mux_8_y, not_1_out, not_2_out, not_3_out,
       not_4_out, not_5_out, not_6_out, not_7_out, not_8_out, not_9_out, pull_resistor_1_node;

  Pull_Resistor pull_resistor_1 (.node(pull_resistor_1_node));
  not not_1 (not_1_out, pull_resistor_1_node);
  not not_2 (not_2_out, in_1);
  _4_1_MUX u_4_1_mux_1 (
    .I0(pull_resistor_1_node), .I1(in_1), .I2(not_2_out), .I3(not_1_out), .Y(n4_1_mux_1_y), .s1(S1), .s0(SQ));
  FULL_ADDER full_adder_1 (.A(in_12), .B(n4_1_mux_1_y), .CIN(full_adder_2_carry), .SUM(S8), .CARRY(full_adder_1_carry));
  not not_3 (not_3_out, in_2);
  _4_1_MUX u_4_1_mux_2 (
    .I0(pull_resistor_1_node), .I1(in_2), .I2(not_3_out), .I3(not_1_out), .Y(n4_1_mux_2_y), .s1(S1), .s0(SQ));
  FULL_ADDER full_adder_2 (.A(in_13), .B(n4_1_mux_2_y), .CIN(full_adder_3_carry), .SUM(S7), .CARRY(full_adder_2_carry));
  not not_4 (not_4_out, in_3);
  _4_1_MUX u_4_1_mux_3 (
    .I0(pull_resistor_1_node), .I1(in_3), .I2(not_4_out), .I3(not_1_out), .Y(n4_1_mux_3_y), .s1(S1), .s0(SQ));
  FULL_ADDER full_adder_3 (.A(in_14), .B(n4_1_mux_3_y), .CIN(full_adder_4_carry), .SUM(S6), .CARRY(full_adder_3_carry));
  not not_5 (not_5_out, in_4);
  _4_1_MUX u_4_1_mux_4 (
    .I0(pull_resistor_1_node), .I1(in_4), .I2(not_5_out), .I3(not_1_out), .Y(n4_1_mux_4_y), .s1(S1), .s0(SQ));
  FULL_ADDER full_adder_4 (.A(A4), .B(n4_1_mux_4_y), .CIN(full_adder_5_carry), .SUM(S5), .CARRY(full_adder_4_carry));
  not not_6 (not_6_out, in_5);
  _4_1_MUX u_4_1_mux_5 (
    .I0(pull_resistor_1_node), .I1(in_5), .I2(not_6_out), .I3(not_1_out), .Y(n4_1_mux_5_y), .s1(S1), .s0(SQ));
  FULL_ADDER full_adder_5 (.A(A3), .B(n4_1_mux_5_y), .CIN(full_adder_6_carry), .SUM(S4), .CARRY(full_adder_5_carry));
  not not_7 (not_7_out, in_6);
  _4_1_MUX u_4_1_mux_6 (
    .I0(pull_resistor_1_node), .I1(in_6), .I2(not_7_out), .I3(not_1_out), .Y(n4_1_mux_6_y), .s1(S1), .s0(SQ));
  FULL_ADDER full_adder_6 (.A(A2), .B(n4_1_mux_6_y), .CIN(full_adder_7_carry), .SUM(S3), .CARRY(full_adder_6_carry));
  not not_8 (not_8_out, in_7);
  _4_1_MUX u_4_1_mux_7 (
    .I0(pull_resistor_1_node), .I1(in_7), .I2(not_8_out), .I3(not_1_out), .Y(n4_1_mux_7_y), .s1(S1), .s0(SQ));
  FULL_ADDER full_adder_7 (.A(A1), .B(n4_1_mux_7_y), .CIN(full_adder_8_carry), .SUM(S1_2), .CARRY(full_adder_7_carry));
  not not_9 (not_9_out, in_8);
  _4_1_MUX u_4_1_mux_8 (
    .I0(pull_resistor_1_node), .I1(in_8), .I2(not_9_out), .I3(not_1_out), .Y(n4_1_mux_8_y), .s1(S1), .s0(SQ));
  FULL_ADDER full_adder_8 (.A(in_19), .B(n4_1_mux_8_y), .CIN(CIN), .SUM(S0), .CARRY(full_adder_8_carry));

  // Notes on the sheet:
  //   M.Yaseen 
endmodule

// FA
module FULL_ADDER (
  input  A,
  input  B,
  input  CIN,
  output SUM,
  output CARRY
);

  wire ha_1_c, ha_1_s, ha_2_c;

  HA ha_1 (.A(A), .B(B), .S(ha_1_s), .C(ha_1_c));
  HA ha_2 (.A(ha_1_s), .B(CIN), .S(SUM), .C(ha_2_c));
  or or_1 (CARRY, ha_2_c, ha_1_c);
endmodule

module HA (
  input  A,
  input  B,
  output S,
  output C
);

  xor xor_1 (S, A, B);
  and and_1 (C, A, B);
endmodule
