// Logisim project LAB5 & 6.circ as structural Verilog: 6 circuits, main circuit 1BIT ALU LAB 5 MAIN
// 1 BIT ALU
module _1BIT_ALU_LAB_5_MAIN (
  input  Ai_1,
  input  Ai_1_2,
  input  B,
  input  A,
  input  s3,
  input  s2,
  input  s1,
  input  s0,
  input  CIN,
  output cout,
  output F
);

  wire design_of_1_bit_arithmetic_logic_shift_unit_1_sum, n1_bit_lu_1_out_5;

  _1_BIT_LU u_1_bit_lu_1 (.out_5(n1_bit_lu_1_out_5), .b(B), .a(A), .S1(s1), .S(s0));
  Design_of_1_bit_Arithmetic_Logic_Shift_Unit design_of_1_bit_arithmetic_logic_shift_unit_1 (
    .B(B), .A(A), .S1(s1), .S0(s0), .cin(CIN), .COUT(cout),
    .SUM(design_of_1_bit_arithmetic_logic_shift_unit_1_sum));
  MUX_4x1 mux_4x1_1 (
    .I0(design_of_1_bit_arithmetic_logic_shift_unit_1_sum), .I1(n1_bit_lu_1_out_5), .I2(Ai_1_2), .I3(Ai_1),
    .Y(F), .S1(s3), .S0(s2));
endmodule

module MUX_4x1 (
  input  S1,
  input  S0,
  input  I0,
  input  I1,
  input  I2,
  input  I3,
  output Y
);

  wire and_1_out, and_2_out, and_3_out, and_4_out, not_1_out, not_2_out;

  not not_1 (not_1_out, S1);
  not not_2 (not_2_out, S0);
  and and_1 (and_1_out, not_2_out, not_1_out, I0);
  and and_2 (and_2_out, S0, not_1_out, I1);
  and and_3 (and_3_out, not_2_out, S1, I2);
  and and_4 (and_4_out, S0, S1, I3);
  or or_1 (Y, and_1_out, and_2_out, and_3_out, and_4_out);
endmodule

module FA (
  input  A,
  input  B,
  input  Cin,
  output Sum,
  output Carry
);

  wire and_1_out, and_2_out, xor_1_out;

  xor xor_1 (xor_1_out, A, B);
  xor xor_2 (Sum, xor_1_out, Cin);
  and and_1 (and_1_out, Cin, xor_1_out);
  and and_2 (and_2_out, A, B);
  or or_1 (Carry, and_1_out, and_2_out);
endmodule

// 1 BIT ALU
module Design_of_1_bit_Arithmetic_Logic_Shift_Unit (
  input  B,
  input  A,
  input  S1,
  input  S0,
  input  cin,
  output COUT,
  output SUM
);

  wire mux_4x1_1_y, not_1_out, not_2_out, pull_resistor_1_node;

  not not_1 (not_1_out, pull_resistor_1_node);
  Pull_Resistor pull_resistor_1 (.node(pull_resistor_1_node));
  not not_2 (not_2_out, B);
  MUX_4x1 mux_4x1_1 (
    .I0(pull_resistor_1_node), .I1(B), .I2(not_2_out), .I3(not_1_out), .Y(mux_4x1_1_y), .S1(S1), .S0(S0));
  FA fa_1 (.A(A), .B(mux_4x1_1_y), .Cin(cin), .Sum(SUM), .Carry(COUT));
endmodule

module _1_BIT_LU (
  input  S1,
  input  S,
  input  b,
  input  a,
  output out_5
);

  wire and_1_out, not_1_out, or_1_out, xor_1_out;

  and and_1 (and_1_out, a, b);
  or or_1 (or_1_out, a, b);
  xor xor_1 (xor_1_out, a, b);
  not not_1 (not_1_out, a);
  MUX_4x1 mux_4x1_1 (.I0(and_1_out), .I1(or_1_out), .I2(xor_1_out), .I3(not_1_out), .Y(out_5), .S1(S1), .S0(S));
endmodule

module _8_BIT_ALU (
  input  [7:0] B,
  input  [7:0] A,
  input  [3:0] S,
  input  cin,
  output [7:0] OUTPUT,
  output out_6
);

  wire n1bit_alu_lab_5_main_2_cout, n1bit_alu_lab_5_main_3_cout, n1bit_alu_lab_5_main_4_cout,
       n1bit_alu_lab_5_main_5_cout, n1bit_alu_lab_5_main_6_cout, n1bit_alu_lab_5_main_7_cout,
       n1bit_alu_lab_5_main_8_cout, pull_resistor_1_node, pull_resistor_2_node;

  Pull_Resistor pull_resistor_1 (.node(pull_resistor_1_node));
  _1BIT_ALU_LAB_5_MAIN u_1bit_alu_lab_5_main_1 (
    .Ai_1(pull_resistor_1_node), .Ai_1_2(A[6]), .B(B[7]), .A(A[7]), .s3(S[3]), .s2(S[2]), .s1(S[1]),
    .s0(S[0]), .CIN(n1bit_alu_lab_5_main_2_cout), .cout(out_6), .F(OUTPUT[7]));
  _1BIT_ALU_LAB_5_MAIN u_1bit_alu_lab_5_main_2 (
    .Ai_1(A[7]), .Ai_1_2(A[5]), .B(B[6]), .A(A[6]), .s3(S[3]), .s2(S[2]), .s1(S[1]), .s0(S[0]),
    .CIN(n1bit_alu_lab_5_main_3_cout), .cout(n1bit_alu_lab_5_main_2_cout), .F(OUTPUT[6]));
  _1BIT_ALU_LAB_5_MAIN u_1bit_alu_lab_5_main_3 (
    .Ai_1(A[6]), .Ai_1_2(A[4]), .B(B[5]), .A(A[5]), .s3(S[3]), .s2(S[2]), .s1(S[1]), .s0(S[0]),
    .CIN(n1bit_alu_lab_5_main_4_cout), .cout(n1bit_alu_lab_5_main_3_cout), .F(OUTPUT[5]));
  _1BIT_ALU_LAB_5_MAIN u_1bit_alu_lab_5_main_4 (
    .Ai_1(A[5]), .Ai_1_2(A[3]), .B(B[4]), .A(A[4]), .s3(S[3]), .s2(S[2]), .s1(S[1]), .s0(S[0]),
    .CIN(n1bit_alu_lab_5_main_5_cout), .cout(n1bit_alu_lab_5_main_4_cout), .F(OUTPUT[4]));
  _1BIT_ALU_LAB_5_MAIN u_1bit_alu_lab_5_main_5 (
    .Ai_1(A[4]), .Ai_1_2(A[2]), .B(B[3]), .A(A[3]), .s3(S[3]), .s2(S[2]), .s1(S[1]), .s0(S[0]),
    .CIN(n1bit_alu_lab_5_main_6_cout), .cout(n1bit_alu_lab_5_main_5_cout), .F(OUTPUT[3]));
  _1BIT_ALU_LAB_5_MAIN u_1bit_alu_lab_5_main_6 (
    .Ai_1(A[3]), .Ai_1_2(A[1]), .B(B[2]), .A(A[2]), .s3(S[3]), .s2(S[2]), .s1(S[1]), .s0(S[0]),
    .CIN(n1bit_alu_lab_5_main_7_cout), .cout(n1bit_alu_lab_5_main_6_cout), .F(OUTPUT[2]));
  _1BIT_ALU_LAB_5_MAIN u_1bit_alu_lab_5_main_7 (
    .Ai_1(A[2]), .Ai_1_2(A[0]), .B(B[1]), .A(A[1]), .s3(S[3]), .s2(S[2]), .s1(S[1]), .s0(S[0]),
    .CIN(n1bit_alu_lab_5_main_8_cout), .cout(n1bit_alu_lab_5_main_7_cout), .F(OUTPUT[1]));
  _1BIT_ALU_LAB_5_MAIN u_1bit_alu_lab_5_main_8 (
    .Ai_1(A[1]), .Ai_1_2(pull_resistor_2_node), .B(B[0]), .A(A[0]), .s3(S[3]), .s2(S[2]), .s1(S[1]),
    .s0(S[0]), .CIN(cin), .cout(n1bit_alu_lab_5_main_8_cout), .F(OUTPUT[0]));
  Pull_Resistor pull_resistor_2 (.node(pull_resistor_2_node));
endmodule
