// Logisim project Lab 01.circ as structural Verilog
module Full_Adder (
  input  A,
  input  B,
  input  Cin,
  output Sum,
  output Carry
);

  wire half_adder_1_c, half_adder_1_s, half_adder_2_c;

  Half_Adder half_adder_1 (.A(A), .B(B), .S(half_adder_1_s), .C(half_adder_1_c));
  Half_Adder half_adder_2 (.A(half_adder_1_s), .B(Cin), .S(Sum), .C(half_adder_2_c));
  or or_1 (Carry, half_adder_2_c, half_adder_1_c);
endmodule

module Half_Adder (
  input  A,
  input  B,
  output S,
  output C
);

  xor xor_1 (S, A, B);
  and and_1 (C, A, B);
endmodule

module _4_bit_Adder (
  input  A3,
  input  A2,
  input  A1,
  input  A0,
  input  Cin,
  input  B3,
  input  B2,
  input  B1,
  input  B0,
  output Cout,
  output S3,
  output S2,
  output S1,
  output S0
);

  wire full_adder_2_carry, full_adder_3_carry, full_adder_4_carry;

  Full_Adder full_adder_1 (.A(A3), .B(B3), .Cin(full_adder_2_carry), .Sum(S3), .Carry(Cout));
  Full_Adder full_adder_2 (.A(A2), .B(B2), .Cin(full_adder_3_carry), .Sum(S2), .Carry(full_adder_2_carry));
  Full_Adder full_adder_3 (.A(A1), .B(B1), .Cin(full_adder_4_carry), .Sum(S1), .Carry(full_adder_3_carry));
  Full_Adder full_adder_4 (.A(A0), .B(B0), .Cin(Cin), .Sum(S0), .Carry(full_adder_4_carry));
endmodule

module _4_Bit_Adder_Subtractor (
  input  B3,
  input  B2,
  input  B1,
  input  B0,
  input  A3,
  input  A2,
  input  A1,
  input  A0,
  input  Cin,
  output Cout,
  output S3,
  output S2,
  output S1,
  output S0
);

  wire xor_1_out, xor_2_out, xor_3_out, xor_4_out;

  xor xor_1 (xor_1_out, B3, Cin);
  xor xor_2 (xor_2_out, B2, Cin);
  xor xor_3 (xor_3_out, B1, Cin);
  xor xor_4 (xor_4_out, B0, Cin);
  _4_bit_Adder u_4_bit_adder_1 (
    .B3(xor_1_out), .A3(A3), .B2(xor_2_out), .A2(A2), .B1(xor_3_out), .A1(A1), .B0(xor_4_out), .A0(A0),
    .Cin(Cin), .Cout(Cout), .S3(S3), .S2(S2), .S1(S1), .S0(S0));
endmodule
