// Logisim project kab7.circ as structural Verilog
// JK FLIP FLOP
module jk (
  input  in_1,
  input  in_2,
  input  in_3,
  output out_4
);

  wire pull_resistor_1_node, pull_resistor_2_node, pull_resistor_3_node;

  J_K_Flip_Flop j_k_ff_1 (
    .J(in_1), .clk(in_2), .K(in_3), .Q(out_4), .preset(pull_resistor_1_node), .en(pull_resistor_3_node),
    .reset(pull_resistor_2_node));  // open: Qn
  Pull_Resistor pull_resistor_1 (.node(pull_resistor_1_node));
  Pull_Resistor pull_resistor_2 (.node(pull_resistor_2_node));
  Pull_Resistor pull_resistor_3 (.node(pull_resistor_3_node));
endmodule

module _4_bit_PC (
  input  CLK,
  input  I3,
  input  I2,
  input  I1,
  input  I0,
  input  INC,
  input  ld,
  output Q3,
  output Q2,
  output Q1,
  output Q0
);

  wire and_1_out, and_2_out, and_3_out, and_4_out, and_5_out, and_6_out, and_7_out, and_8_out, and_9_out,
       and_10_out, and_11_out, and_12_out, and_13_out, clock_1_out, not_1_out, not_2_out, not_3_out,
       not_4_out, not_5_out, not_6_out, or_1_out, or_2_out, or_3_out, or_4_out, or_5_out, or_6_out, or_7_out,
       or_8_out;

  not not_1 (not_1_out, I3);
  and and_1 (and_1_out, not_1_out, and_13_out);
  and and_2 (and_2_out, I3, and_13_out);
  or or_1 (or_1_out, and_1_out, and_3_out, CLK);
  jk jk_1 (.in_1(or_2_out), .in_2(clock_1_out), .in_3(or_1_out), .out_4(Q3));
  and and_3 (and_3_out, and_6_out, Q2);
  or or_2 (or_2_out, and_2_out, and_3_out);
  not not_2 (not_2_out, I2);
  and and_4 (and_4_out, not_2_out, and_13_out);
  or or_3 (or_3_out, and_4_out, and_6_out, CLK);
  jk jk_2 (.in_1(or_4_out), .in_2(clock_1_out), .in_3(or_3_out), .out_4(Q2));
  and and_5 (and_5_out, I2, and_13_out);
  or or_4 (or_4_out, and_5_out, and_6_out);
  and and_6 (and_6_out, and_9_out, Q1);
  not not_3 (not_3_out, I1);
  and and_7 (and_7_out, not_3_out, and_13_out);
  or or_5 (or_5_out, and_7_out, and_9_out, CLK);
  and and_8 (and_8_out, I1, and_13_out);
  or or_6 (or_6_out, and_8_out, and_9_out);
  jk jk_3 (.in_1(or_6_out), .in_2(clock_1_out), .in_3(or_5_out), .out_4(Q1));
  and and_9 (and_9_out, and_12_out, Q0);
  not not_4 (not_4_out, I0);
  and and_10 (and_10_out, not_4_out, and_13_out);
  and and_11 (and_11_out, I0, and_13_out);
  or or_7 (or_7_out, and_10_out, and_12_out, CLK);
  jk jk_4 (.in_1(or_8_out), .in_2(clock_1_out), .in_3(or_7_out), .out_4(Q0));
  not not_5 (not_5_out, ld);
  and and_12 (and_12_out, INC, not_5_out, not_6_out);
  or or_8 (or_8_out, and_11_out, and_12_out);
  Clock clock_1 (.out(clock_1_out));
  not not_6 (not_6_out, CLK);
  and and_13 (and_13_out, ld, not_6_out);
endmodule
