// Logisim project lab 4.circ as structural Verilog: 2 circuits, main circuit 2-1 MUX
// 2-1 mux
module _2_1_MUX (
  input  s0,
  input  I0,
  input  I1,
  output y
);

  wire and_1_out, and_2_out, not_1_out;

  not not_1 (not_1_out, s0);
  and and_1 (and_1_out, not_1_out, I0);
  and and_2 (and_2_out, s0, I1);
  or or_1 (y, and_1_out, and_2_out);
endmodule

module _8_bit_shifter (
  input  [7:0] in_1,
  input  in_2,
  output [7:0] out_3
);

  wire pull_resistor_1_node, pull_resistor_2_node;

  Pull_Resistor pull_resistor_1 (.node(pull_resistor_1_node));
  _2_1_MUX u_2_1_mux_1 (.s0(in_2), .I0(pull_resistor_1_node), .I1(in_1[6]), .y(out_3[7]));
  _2_1_MUX u_2_1_mux_2 (.s0(in_2), .I0(in_1[7]), .I1(in_1[5]), .y(out_3[6]));
  _2_1_MUX u_2_1_mux_3 (.s0(in_2), .I0(in_1[6]), .I1(in_1[4]), .y(out_3[5]));
  _2_1_MUX u_2_1_mux_4 (.s0(in_2), .I0(in_1[5]), .I1(in_1[3]), .y(out_3[4]));
  _2_1_MUX u_2_1_mux_5 (.s0(in_2), .I0(in_1[4]), .I1(in_1[2]), .y(out_3[3]));
  _2_1_MUX u_2_1_mux_6 (.s0(in_2), .I0(in_1[3]), .I1(in_1[1]), .y(out_3[2]));
  _2_1_MUX u_2_1_mux_7 (.s0(in_2), .I0(in_1[2]), .I1(in_1[0]), .y(out_3[1]));
  Pull_Resistor pull_resistor_2 (.node(pull_resistor_2_node));
  _2_1_MUX u_2_1_mux_8 (.s0(in_2), .I0(in_1[1]), .I1(pull_resistor_2_node), .y(out_3[0]));
endmodule
