// Logisim project lab1.circ as structural Verilog
// FA
module adder (
  input  a,
  input  b,
  input  C_in,
  output SUM,
  output Cout
);

  wire and_1_out, and_2_out, xor_1_out;

  xor xor_1 (xor_1_out, a, b);
  and and_1 (and_1_out, a, b);
  xor xor_2 (SUM, xor_1_out, C_in);
  and and_2 (and_2_out, xor_1_out, C_in);
  or or_1 (Cout, and_1_out, and_2_out);
endmodule
