// Logisim project lab3.circ as structural Verilog: 3 circuits, main circuit 1 bit lu
// 1 BIT LU
module _1_bit_lu (
  input  A,
  input  B,
  input  S1,
  input  S0,
  output out_5
);

  wire and_1_out, not_1_out, or_1_out, xor_1_out;

  and and_1 (and_1_out, A, B);
  or or_1 (or_1_out, B, A);
  xor xor_1 (xor_1_out, B, A);
  not not_1 (not_1_out, A);
  _4_1_MUX u_4_1_mux_1 (.I0(and_1_out), .I1(or_1_out), .I2(xor_1_out), .I3(not_1_out), .Y(out_5), .s1(S1), .s0(S0));
endmodule

module lab3 (
  input  B7,
  input  B6,
  input  B5,
  input  B4,
  input  B3,
  input  B2,
  input  B1,
  input  B0,
  input  A6,
  input  A7,
  input  A5,
  input  A4,
  input  A3,
  input  A2,
  input  A1,
  input  A0,
  input  s1,
  input  s0,
  output out_19,
  output out_20,
  output out_21,
  output out_22,
  output out_23,
  output out_24,
  output out_25,
  output out_26
);

  _1_bit_lu u_1_bit_lu_1 (.B(B7), .A(A7), .S1(s1), .S0(s0), .out_5(out_19));
  _1_bit_lu u_1_bit_lu_2 (.B(B6), .A(A6), .S1(s1), .S0(s0), .out_5(out_20));
  _1_bit_lu u_1_bit_lu_3 (.B(B5), .A(A5), .S1(s1), .S0(s0), .out_5(out_21));
  _1_bit_lu u_1_bit_lu_4 (.B(B4), .A(A4), .S1(s1), .S0(s0), .out_5(out_22));
  _1_bit_lu u_1_bit_lu_5 (.B(B3), .A(A3), .S1(s1), .S0(s0), .out_5(out_23));
  _1_bit_lu u_1_bit_lu_6 (.B(B2), .A(A2), .S1(s1), .S0(s0), .out_5(out_24));
  _1_bit_lu u_1_bit_lu_7 (.B(B1), .A(A1), .S1(s1), .S0(s0), .out_5(out_25));
  _1_bit_lu u_1_bit_lu_8 (.B(B0), .A(A0), .S1(s1), .S0(s0), .out_5(out_26));
endmodule

module _4_1_MUX (
  input  s1,
  input  s0,
  input  I0,
  input  I1,
  input  I2,
  input  I3,
  output Y
);

  wire and_1_out, and_2_out, and_3_out, and_4_out, not_1_out, not_2_out;

  not not_1 (not_1_out, s1);
  not not_2 (not_2_out, s0);
  and and_1 (and_1_out, not_2_out, not_1_out, I0);
  and and_2 (and_2_out, s0, not_1_out, I1);
  and and_3 (and_3_out, not_2_out, s1, I2);
  and and_4 (and_4_out, s0, s1, I3);
  or or_1 (Y, and_1_out, and_2_out, and_4_out, and_3_out);
endmodule
